# Fritzing sketch Bryce (saved by Fritzing 0.9.3b)
circuit board: 5cm x 8.5cm
breadboards: 1

parts:
  SEL = Pushbutton [package="[THT]"]
  L = Pushbutton [package="[THT]"]
  U = Pushbutton [package="[THT]"]
  R = Pushbutton [package="[THT]"]
  D = Pushbutton [package="[THT]"]
  10K = Resistor [tolerance=±5% resistance=10k package=THT]
  10K_2 = Resistor [tolerance=±5% resistance=10k package=THT]
  10K_3 = Resistor [tolerance=±5% resistance=10k package=THT]
  10K_4 = Resistor [tolerance=±5% resistance=10k package=THT]
  10K_5 = Resistor [tolerance=±5% resistance=10k package=THT]
  +SPK- = Piezo Speaker
  D_+_- = female pin header, 3 pins [form="♀ (female)"]
  -_+_x_x_x_R_A_D_C_S_x_O_I_x_+_- = female pin header, 16 pins [form="♀ (female)"]
  PHOTO = Photocell (LDR) [package=THT]
  10K_6 = Resistor [tolerance=±5% resistance=10k package=THT]
  ARDUINO = Arduino Pro Mini v13
  +_- = female pin header, 2 pins [form="♀ (female)"]
  I/O = Toggle Switch [package=THT]

nets:
  N1: SEL.Pin_1, SEL.Pin_2, D_+_-.pin2
  N2: SEL.Pin_3, SEL.Pin_4, L.Pin_1, U.Pin_2, R.Pin_2, D.Pin_1, D.Pin_2, 10K_3.Pin_1, -_+_x_x_x_R_A_D_C_S_x_O_I_x_+_-.pin2, -_+_x_x_x_R_A_D_C_S_x_O_I_x_+_-.pin15, 10K_6.Pin_1, ARDUINO.VCC, ARDUINO.D2
  N3: L.Pin_3, L.Pin_4, 10K_2.Pin_1, ARDUINO.D7
  N4: U.Pin_3, U.Pin_4, 10K.Pin_1, ARDUINO.D6_PWM
  N5: R.Pin_3, R.Pin_4, 10K_4.Pin_1, ARDUINO.D5_PWM
  N6: D.Pin_3, D.Pin_4, 10K_5.Pin_1, ARDUINO.D4
  N7: 10K.Pin_0, 10K_2.Pin_0, 10K_3.Pin_0, 10K_4.Pin_0, 10K_5.Pin_0, +SPK-.pin1, D_+_-.pin3, -_+_x_x_x_R_A_D_C_S_x_O_I_x_+_-.pin1, -_+_x_x_x_R_A_D_C_S_x_O_I_x_+_-.pin16, PHOTO.pin_0, ARDUINO.GND, +_-.pin2
  N8: +SPK-.pin2, ARDUINO.D12/MISO
  N9: D_+_-.pin1, ARDUINO.D3_PWM
  N10: -_+_x_x_x_R_A_D_C_S_x_O_I_x_+_-.pin6, ARDUINO.D9_PWM
  N11: -_+_x_x_x_R_A_D_C_S_x_O_I_x_+_-.pin8, ARDUINO.D8
  N12: -_+_x_x_x_R_A_D_C_S_x_O_I_x_+_-.pin9, ARDUINO.D13/SCK
  N13: -_+_x_x_x_R_A_D_C_S_x_O_I_x_+_-.pin10, ARDUINO.D10_PWM/SS
  N14: -_+_x_x_x_R_A_D_C_S_x_O_I_x_+_-.pin13, ARDUINO.D11_PWM/MOSI
  N15: PHOTO.pin_1, 10K_6.Pin_0
  N16: ARDUINO.RAW, I/O.COM, I/O.L2
  N17: +_-.pin1, I/O.L1

notes:
  Berrygotchi
